# Fritzing sketch OpenPBRv0.2 (saved by Fritzing 0.9.3b)

parts:
  Bauteil1 = Arduino Mega 2560 (Rev3)
  U5 = Voltage Regulator [package=to220-adj]
  R24 = Resistor [tolerance=±5% resistance=330 package=THT]
  R25 = Resistor [tolerance=±5% resistance=1k package=THT]
  Q1 = Basic FET N-Channel [package="TO220 [THT]"]
  Q2 = Basic FET N-Channel [package="TO220 [THT]"]
  Q3 = Basic FET N-Channel [package="TO220 [THT]"]
  Q4 = Basic FET N-Channel [package="TO220 [THT]"]
  Q5 = Basic FET N-Channel [package="TO220 [THT]"]
  Q6 = Basic FET N-Channel [package="TO220 [THT]"]
  Q7 = Basic FET N-Channel [package="TO220 [THT]"]
  Q8 = Basic FET N-Channel [package="TO220 [THT]"]
  Q9 = Basic FET N-Channel [package="TO220 [THT]"]
  Q10 = Basic FET N-Channel [package="TO220 [THT]"]
  Q11 = Basic FET N-Channel [package="TO220 [THT]"]
  R26 = Resistor [tolerance=±5% resistance=100 package=THT]
  R27 = Resistor [tolerance=±5% resistance=100 package=THT]
  R28 = Resistor [tolerance=±5% resistance=100 package=THT]
  R29 = Resistor [tolerance=±5% resistance=100 package=THT]
  R30 = Resistor [tolerance=±5% resistance=100 package=THT]
  R31 = Resistor [tolerance=±5% resistance=100 package=THT]
  R32 = Resistor [tolerance=±5% resistance=100 package=THT]
  R33 = Resistor [tolerance=±5% resistance=100 package=THT]
  R34 = Resistor [tolerance=±5% resistance=100 package=THT]
  R35 = Resistor [tolerance=±5% resistance=100 package=THT]
  R36 = Resistor [tolerance=±5% resistance=100 package=THT]
  M1 = DC Motor
  M2 = DC Motor
  M3 = DC Motor
  M4 = DC Motor
  LED1 = LED - 5mm [color="White (6500K)" package="5 mm [THT]"]
  LED2 = LED - 5mm [color="Blue (525nm)" package="5 mm [THT]"]
  LED3 = LED - 5mm [color="Red (633nm)" package="5 mm [THT]"]
  LED4 = LED - 5mm [color="Green (570nm)" package="5 mm [THT]"]
  L1 = Solenoid
  R37 = Resistor [tolerance=±5% resistance=220 package=THT]
  M5 = DC Motor
  M6 = DC Motor
  R38 = PHOTOCELL [package=photocell-kit]
  R39 = PHOTOCELL [package=photocell-kit]
  R40 = PHOTOCELL [package=photocell-kit]
  R41 = Resistor [tolerance=±5% resistance=20 package=THT]
  R42 = Resistor [tolerance=±5% resistance=20 package=THT]
  R43 = Resistor [tolerance=±5% resistance=20 package=THT]
  LED5 = LED - 5mm [color="Red (660nm)" package="5 mm [THT]"]
  LED6 = LED - 5mm [color="Red (660nm)" package="5 mm [THT]"]
  LED7 = LED - 5mm [color="Red (660nm)" package="5 mm [THT]"]
  R44 = Resistor [tolerance=±5% resistance=30 package=THT]
  T2 = LM35 Temperature Sensor [package="TO92 [THT]"]
  R45 = Resistor [tolerance=±5% resistance=5k package=THT]

nets:
  N1: Bauteil1.A1, R38.P$1
  N2: Bauteil1.A2, R38.P$2, R41.Pin_0
  N3: Bauteil1.A3, R39.P$1
  N4: Bauteil1.A4, R39.P$2, R43.Pin_0
  N5: Bauteil1.A5, R40.P$1
  N6: Bauteil1.A6, R40.P$2, R42.Pin_0
  N7: Bauteil1.D17_PWM/RX2, LED7.cathode
  N8: Bauteil1.D16_PWM/TX2, LED6.cathode
  N9: Bauteil1.D15/RX3, LED5.cathode
  GND: Bauteil1.GND, R25.Pin_1, M1.pin_2, M2.pin_2, M3.pin_2, M4.pin_2, LED1.cathode, LED2.cathode, LED3.cathode, LED4.cathode, L1.pin1, M5.pin_2, M6.pin_2, R44.Pin_1, T2.GND
  N10: Bauteil1.D13_PWM, T2.Vout, R45.Pin_1
  N11: Bauteil1.D12_PWM, R34.Pin_0
  N12: Bauteil1.D11_PWM, R35.Pin_0
  N13: Bauteil1.D10_PWM, R36.Pin_0
  N14: Bauteil1.D9_PWM, R27.Pin_0
  N15: Bauteil1.D8_PWM, R28.Pin_0
  N16: Bauteil1.D2_PWM, R30.Pin_0
  N17: Bauteil1.D3_PWM, R33.Pin_0
  N18: Bauteil1.D4_PWM, R32.Pin_0
  N19: Bauteil1.D5_PWM, R31.Pin_0
  N20: Bauteil1.D6_PWM, R26.Pin_0
  N21: Bauteil1.D7_PWM, R29.Pin_0
  N22: U5.ADJ, R24.Pin_0, R37.Pin_0
  12V: U5.IN, Q1.source, Q2.source, Q3.source, Q4.source, Q5.source
  N23: U5.OUT, Q6.source, Q7.source, Q8.source, Q9.source, Q10.source, Q11.source, R37.Pin_1, R41.Pin_1, R42.Pin_1, R43.Pin_1, T2.+Vs, R45.Pin_0
  N24: R24.Pin_1, R25.Pin_0
  N25: Q1.gate, R30.Pin_1
  N26: Q1.drain, L1.pin2
  N27: Q2.gate, R26.Pin_1
  N28: Q2.drain, LED4.anode
  N29: Q3.gate, R31.Pin_1
  N30: Q3.drain, LED2.anode
  N31: Q4.gate, R33.Pin_1
  N32: Q4.drain, LED1.anode
  N33: Q5.gate, R32.Pin_1
  N34: Q5.drain, LED3.anode
  N35: Q6.gate, R29.Pin_1
  N36: Q6.drain, M4.pin_1
  N37: Q7.gate, R28.Pin_1
  N38: Q7.drain, M3.pin_1
  N39: Q8.gate, R27.Pin_1
  N40: Q8.drain, M2.pin_1
  N41: Q9.gate, R36.Pin_1
  N42: Q9.drain, M6.pin_1
  N43: Q10.gate, R35.Pin_1
  N44: Q10.drain, M1.pin_1
  N45: Q11.gate, R34.Pin_1
  N46: Q11.drain, M5.pin_1
  N47: LED5.anode, LED6.anode, LED7.anode, R44.Pin_0
